// Logisim project arithmeticKP.circ as structural Verilog: 8 circuits, main circuit add1
module add1 (
  input  Ai,
  input  Bi,
  input  Cin,
  output Si,
  output Cout
);

  wire and_1_out, and_2_out, and_3_out, and_4_out, and_5_out, and_6_out, and_7_out, and_8_out;

  and and_1 (and_1_out, Ai, Bi, Cin);
  and and_2 (and_2_out, Ai, Bi, ~Cin);  // AND_Gate
  or or_1 (Cout, and_1_out, and_2_out, and_3_out, and_5_out);
  and and_3 (and_3_out, Ai, ~Bi, Cin);  // AND_Gate
  and and_4 (and_4_out, Ai, ~Bi, ~Cin);  // AND_Gate
  and and_5 (and_5_out, ~Ai, Bi, Cin);  // AND_Gate
  and and_6 (and_6_out, ~Ai, Bi, ~Cin);  // AND_Gate
  and and_7 (and_7_out, ~Ai, ~Bi, Cin);  // AND_Gate
  or or_2 (Si, and_1_out, and_4_out, and_6_out, and_7_out);
  and and_8 (and_8_out, ~Ai, ~Bi, ~Cin);  // AND_Gate
endmodule

module add8 (
  input  [7:0] in_1,
  input  [7:0] in_2,
  output [7:0] out_3
);

  wire add1_2_cout, add1_3_cout, add1_4_cout, add1_5_cout, add1_6_cout, add1_7_cout, add1_8_cout;

  add1 add1_1 (.Ai(in_2[7]), .Bi(in_1[7]), .Si(out_3[7]), .Cin(add1_2_cout));  // open: Cout
  Hex_Digit_Display hex_digit_display_1 (.value(in_2[7:4]));  // open: dp
  Hex_Digit_Display hex_digit_display_2 (.value(in_2[3:0]));  // open: dp
  add1 add1_2 (.Cout(add1_2_cout), .Ai(in_2[6]), .Bi(in_1[6]), .Si(out_3[6]), .Cin(add1_3_cout));
  add1 add1_3 (.Cout(add1_3_cout), .Ai(in_2[5]), .Bi(in_1[5]), .Si(out_3[5]), .Cin(add1_4_cout));
  add1 add1_4 (.Cout(add1_4_cout), .Ai(in_2[4]), .Bi(in_1[4]), .Si(out_3[4]), .Cin(add1_5_cout));
  add1 add1_5 (.Cout(add1_5_cout), .Ai(in_2[3]), .Bi(in_1[3]), .Si(out_3[3]), .Cin(add1_6_cout));
  add1 add1_6 (.Cout(add1_6_cout), .Ai(in_2[2]), .Bi(in_1[2]), .Si(out_3[2]), .Cin(add1_7_cout));
  add1 add1_7 (.Cout(add1_7_cout), .Ai(in_2[1]), .Bi(in_1[1]), .Si(out_3[1]), .Cin(add1_8_cout));
  Hex_Digit_Display hex_digit_display_3 (.value(out_3[7:4]));  // open: dp
  Hex_Digit_Display hex_digit_display_4 (.value(in_1[7:4]));  // open: dp
  add1 add1_8 (.Cout(add1_8_cout), .Ai(in_2[0]), .Bi(in_1[0]), .Si(out_3[0]), .Cin(1'b0));
  Hex_Digit_Display hex_digit_display_5 (.value(out_3[3:0]));  // open: dp
  Hex_Digit_Display hex_digit_display_6 (.value(in_1[3:0]));  // open: dp
endmodule

module mux8 (
  input  A,
  input  B,
  input  [7:0] in_3,
  input  [7:0] in_4,
  input  [7:0] in_5,
  input  [7:0] in_6,
  input  S,
  input  [1:0] in_8,
  output Out,
  output [7:0] out_10
);

  wire and_5_out, and_6_out;
  wire [7:0] and_1_out, and_2_out, and_3_out, and_4_out, selector_1_out_2, selector_1_out_3;

  assign and_1_out = in_3 & selector_1_out_3 & selector_1_out_2;  // AND_Gate and_1, 8 bits wide
  Hex_Digit_Display hex_digit_display_1 (.value(in_3[7:4]));  // open: dp
  Hex_Digit_Display hex_digit_display_2 (.value(in_3[3:0]));  // open: dp
  assign and_2_out = in_4 & selector_1_out_3 & ~selector_1_out_2;  // AND_Gate and_2, 8 bits wide
  Hex_Digit_Display hex_digit_display_3 (.value(in_4[7:4]));  // open: dp
  Hex_Digit_Display hex_digit_display_4 (.value(in_4[3:0]));  // open: dp
  assign out_10 = and_1_out | and_2_out | and_3_out | and_4_out;  // OR_Gate or_1, 8 bits wide
  Hex_Digit_Display hex_digit_display_5 (.value(in_5[7:4]));  // open: dp
  assign and_3_out = in_5 & ~selector_1_out_3 & selector_1_out_2;  // AND_Gate and_3, 8 bits wide
  Hex_Digit_Display hex_digit_display_6 (.value(out_10[7:4]));  // open: dp
  Hex_Digit_Display hex_digit_display_7 (.value(in_5[3:0]));  // open: dp
  Hex_Digit_Display hex_digit_display_8 (.value(out_10[3:0]));  // open: dp
  Hex_Digit_Display hex_digit_display_9 (.value(in_6[7:4]));  // open: dp
  assign and_4_out = in_6 & ~selector_1_out_3 & ~selector_1_out_2;  // AND_Gate and_4, 8 bits wide
  Hex_Digit_Display hex_digit_display_10 (.value(in_6[3:0]));  // open: dp
  selector selector_1 (.out_2(selector_1_out_2), .out_3(selector_1_out_3), .in_1(in_8));
  and and_5 (and_5_out, A, ~S);  // AND_Gate
  and and_6 (and_6_out, B, S);
  or or_2 (Out, and_5_out, and_6_out);

  // Notes on the sheet:
  //   multiplexerKP
  //   Warmup
endmodule

module selector (
  input  [1:0] in_1,
  output [7:0] out_2,
  output [7:0] out_3
);


  assign out_2 = {8{in_1[0]}};
  assign out_3 = {8{in_1[1]}};
endmodule

module neg8 (
  input  [7:0] in_1,
  output [7:0] out_2
);

  wire [7:0] not_1_out;

  Hex_Digit_Display hex_digit_display_1 (.value(in_1[7:4]));  // open: dp
  Hex_Digit_Display hex_digit_display_2 (.value(in_1[3:0]));  // open: dp
  assign not_1_out = ~in_1;  // NOT_Gate not_1, 8 bits wide
  add8 add8_1 (.in_2(not_1_out), .in_1(8'h1), .out_3(out_2));
endmodule

module sub8 (
  input  [7:0] in_1,
  input  [7:0] in_2,
  output [7:0] out_3
);

  wire [7:0] neg8_1_out_2;

  Hex_Digit_Display hex_digit_display_1 (.value(in_1[7:4]));  // open: dp
  Hex_Digit_Display hex_digit_display_2 (.value(in_1[3:0]));  // open: dp
  add8 add8_1 (.in_2(in_1), .in_1(neg8_1_out_2), .out_3(out_3));
  neg8 neg8_1 (.in_1(in_2), .out_2(neg8_1_out_2));
  Hex_Digit_Display hex_digit_display_3 (.value(out_3[7:4]));  // open: dp
  Hex_Digit_Display hex_digit_display_4 (.value(out_3[3:0]));  // open: dp
  Hex_Digit_Display hex_digit_display_5 (.value(in_2[7:4]));  // open: dp
  Hex_Digit_Display hex_digit_display_6 (.value(in_2[3:0]));  // open: dp
endmodule

module mul2 (
  input  [7:0] in_1,
  output [7:0] out_2
);

  Hex_Digit_Display hex_digit_display_1 (.value(in_1[7:4]));  // open: dp
  Hex_Digit_Display hex_digit_display_2 (.value(in_1[3:0]));  // open: dp
  Hex_Digit_Display hex_digit_display_3 (.value(in_1[6:3]));  // open: dp
  Hex_Digit_Display hex_digit_display_4 (.value({in_1[2:0], 1'b0}));  // open: dp

  assign out_2 = {in_1[6:0], 1'b0};
endmodule

module div2 (
  input  [7:0] in_1,
  output [7:0] out_2
);

  Hex_Digit_Display hex_digit_display_1 (.value(in_1[7:4]));  // open: dp
  Hex_Digit_Display hex_digit_display_2 (.value(in_1[3:0]));  // open: dp
  Hex_Digit_Display hex_digit_display_3 (.value({{2{in_1[7]}}, in_1[6:5]}));  // open: dp
  Hex_Digit_Display hex_digit_display_4 (.value(in_1[4:1]));  // open: dp

  assign out_2 = {{2{in_1[7]}}, in_1[6:1]};
endmodule
