// Logisim project decoderKP.circ as structural Verilog: 2 circuits, main circuit decode
// d
module decode (
  input  A,
  input  B,
  output out_3,
  output out_4,
  output out_5,
  output out_6
);

  and and_1 (out_3, ~A, ~B);  // AND_Gate
  and and_2 (out_4, A, ~B);  // AND_Gate
  and and_3 (out_5, ~A, B);  // AND_Gate
  and and_4 (out_6, A, B);

  // Notes on the sheet:
  //   decoderKP
  //   2-input decoder
endmodule

module newCircuit (
  input  in_1,
  input  in_2,
  input  in_3,
  input  in_4,
  output out_5,
  output out_6,
  output out_7,
  output out_8,
  output out_9,
  output out_10,
  output out_11,
  output out_12
);

  decode decode_1 (.A(in_1), .B(in_2), .out_3(out_5), .out_4(out_6), .out_5(out_7), .out_6(out_8));
  decode decode_2 (.A(in_3), .B(in_4), .out_3(out_9), .out_4(out_10), .out_5(out_11), .out_6(out_12));
endmodule
