// Logisim project gatesKP.circ as structural Verilog: 1 circuit, main circuit main
module main (
  input  in_1,
  input  in_2,
  input  in_3,
  input  in_4,
  input  in_5,
  input  A,
  input  B,
  input  A_2,
  input  B_2,
  input  C,
  input  A_3,
  input  B_3,
  input  C_2,
  output out_14,
  output out_15,
  output out_16,
  output Z,
  output Z_2,
  output Y
);

  wire and_1_out, and_2_out, and_3_out, and_4_out, not_1_out, not_2_out, or_1_out, or_2_out, or_3_out,
       or_4_out;

  and u_A (out_14, in_1, in_4);
  and and_1 (and_1_out, A, B);
  or or_1 (or_1_out, A, B);
  not not_1 (not_1_out, A_2);
  and and_2 (and_2_out, B_3, C_2);
  not not_2 (not_2_out, and_1_out);
  and and_3 (and_3_out, not_1_out, B_2);
  or or_2 (or_2_out, A_2, C);
  or or_3 (or_3_out, A_3, and_2_out);
  not not_3 (Y, or_3_out);
  or u_B (out_15, in_2, in_5);
  and and_4 (and_4_out, B_2, or_2_out);
  and and_5 (Z, not_2_out, or_1_out);
  or or_4 (or_4_out, and_3_out, and_4_out);
  not u_C (out_16, in_3);
  and and_6 (Z_2, or_4_out, and_4_out);

  // Notes on the sheet:
  //   XOR
  //   Y = NOT(A OR (B AND C))
  //   XOR and More by KP
  //   Gates by KP
  //   Z = (((NOT A AND B) OR (B AND (A OR C)) AND (B AND (A OR C)))
endmodule
