// Logisim project machineKP.circ as structural Verilog: 4 circuits, main circuit blinky
module blinky (
  input  in_1
);

  wire and_1_out, clock_1_out, flipflop_1_out_3;

  Clock clock_1 (.out(clock_1_out));
  and and_1 (and_1_out, in_1, ~flipflop_1_out_3);  // AND_Gate
  flipflop flipflop_1 (.out_3(flipflop_1_out_3), .in_2(clock_1_out), .in_1(and_1_out));
  LED led_1 (.in(and_1_out));
endmodule

module flipflop (
  input  in_1,
  input  in_2,
  output out_3
);

  wire and_1_out, and_2_out, and_3_out, and_4_out, and_5_out, and_6_out, and_7_out, and_8_out, not_2_out,
       not_3_out, not_4_out, not_5_out, not_6_out, not_7_out, not_8_out, not_9_out;

  not not_1 (out_3, and_1_out);
  not not_2 (not_2_out, and_2_out);
  and and_1 (and_1_out, not_3_out, not_2_out);
  and and_2 (and_2_out, out_3, not_4_out);
  not not_3 (not_3_out, and_3_out);
  and and_3 (and_3_out, not_5_out, in_2);
  not not_4 (not_4_out, and_4_out);
  and and_4 (and_4_out, in_2, ~not_5_out);  // AND_Gate
  not not_5 (not_5_out, and_5_out);
  not not_6 (not_6_out, and_6_out);
  and and_5 (and_5_out, not_8_out, not_6_out);
  and and_6 (and_6_out, not_5_out, not_9_out);
  not not_7 (not_7_out, in_2);
  not not_8 (not_8_out, and_7_out);
  and and_7 (and_7_out, in_1, not_7_out);
  not not_9 (not_9_out, and_8_out);
  and and_8 (and_8_out, not_7_out, ~in_1);  // AND_Gate
endmodule

module \logic  (
  input  in_1,
  input  in_2,
  input  in_3,
  output out_4,
  output out_5,
  output out_6,
  output out_7,
  output out_8
);

  wire and_1_out, and_2_out, and_3_out;

  and and_1 (and_1_out, in_1, ~in_2, ~in_3);  // AND_Gate
  and and_2 (and_2_out, in_1, ~in_2, in_3);  // AND_Gate
  and and_3 (and_3_out, in_1, in_2, ~in_3);  // AND_Gate
  and and_4 (out_6, in_1, in_2, in_3);
  or or_1 (out_4, and_2_out, and_3_out, out_6);
  or or_2 (out_5, and_3_out, out_6);
  or or_3 (out_7, and_2_out, and_3_out);
  or or_4 (out_8, and_3_out, and_1_out);
endmodule

module danger (
  input  in_1
);

  wire clock_1_out, flipflop_1_out_3, flipflop_2_out_3, logic_1_out_4, logic_1_out_5, logic_1_out_6,
       logic_1_out_7, logic_1_out_8;

  Clock clock_1 (.out(clock_1_out));
  \logic  logic_1 (
    .in_1(in_1), .in_2(flipflop_2_out_3), .in_3(flipflop_1_out_3), .out_4(logic_1_out_4),
    .out_5(logic_1_out_5), .out_6(logic_1_out_6), .out_7(logic_1_out_7), .out_8(logic_1_out_8));
  flipflop flipflop_1 (.out_3(flipflop_1_out_3), .in_2(clock_1_out), .in_1(logic_1_out_8));
  flipflop flipflop_2 (.out_3(flipflop_2_out_3), .in_2(clock_1_out), .in_1(logic_1_out_7));
  LED led_1 (.in(logic_1_out_4));
  LED led_2 (.in(logic_1_out_5));
  LED led_3 (.in(logic_1_out_5));
  LED led_4 (.in(logic_1_out_4));
  LED led_5 (.in(logic_1_out_6));

  // Notes on the sheet:
  //   1
  //   2
  //   3
  //   4
  //   5
endmodule
