// Logisim project memoryKP.circ as structural Verilog: 4 circuits, main circuit bit
module \bit  (
  input  D,
  input  WE,
  output Q
);

  wire and_1_out, and_2_out, and_3_out, and_4_out, not_1_out, not_2_out, not_4_out;

  and and_1 (and_1_out, D, WE);
  and and_2 (and_2_out, WE, ~D);  // AND_Gate
  not not_1 (not_1_out, and_2_out);
  not not_2 (not_2_out, and_1_out);
  and and_3 (and_3_out, not_2_out, not_4_out);
  not not_3 (Q, and_3_out);
  and and_4 (and_4_out, Q, not_1_out);
  not not_4 (not_4_out, and_4_out);

  // Notes on the sheet:
  //   S
  //   R
endmodule

module \byte  (
  input  WE,
  input  [7:0] in_2,
  input  A,
  output [7:0] out_4
);

  wire and_1_out, bit_1_q, bit_2_q, bit_3_q, bit_4_q, bit_5_q, bit_6_q, bit_7_q, bit_8_q;

  and and_1 (and_1_out, A, WE);
  \bit  bit_1 (.D(in_2[7]), .WE(and_1_out), .Q(bit_1_q));
  and and_2 (out_4[7], bit_1_q, A);
  \bit  bit_2 (.D(in_2[6]), .WE(and_1_out), .Q(bit_2_q));
  and and_3 (out_4[6], bit_2_q, A);
  \bit  bit_3 (.D(in_2[5]), .WE(and_1_out), .Q(bit_3_q));
  and and_4 (out_4[5], bit_3_q, A);
  \bit  bit_4 (.D(in_2[4]), .WE(and_1_out), .Q(bit_4_q));
  and and_5 (out_4[4], bit_4_q, A);
  \bit  bit_5 (.D(in_2[3]), .WE(and_1_out), .Q(bit_5_q));
  and and_6 (out_4[3], bit_5_q, A);
  \bit  bit_6 (.D(in_2[2]), .WE(and_1_out), .Q(bit_6_q));
  and and_7 (out_4[2], bit_6_q, A);
  \bit  bit_7 (.D(in_2[1]), .WE(and_1_out), .Q(bit_7_q));
  and and_8 (out_4[1], bit_7_q, A);
  \bit  bit_8 (.D(in_2[0]), .WE(and_1_out), .Q(bit_8_q));
  and and_9 (out_4[0], bit_8_q, A);
endmodule

module bank4 (
  input  WE,
  input  [7:0] in_2,
  input  [1:0] A,
  input  b,
  output [7:0] out_5
);

  wire and_1_out, and_2_out, and_3_out, and_4_out;
  wire [7:0] byte_1_out_4, byte_2_out_4, byte_3_out_4, byte_4_out_4;

  and and_1 (and_1_out, ~A[0], ~A[1], b);  // AND_Gate
  and and_2 (and_2_out, A[0], ~A[1], b);  // AND_Gate
  and and_3 (and_3_out, ~A[0], A[1], b);  // AND_Gate
  and and_4 (and_4_out, A[0], A[1], b);
  \byte  byte_1 (.A(and_1_out), .WE(WE), .in_2(in_2), .out_4(byte_1_out_4));
  \byte  byte_2 (.A(and_2_out), .WE(WE), .in_2(in_2), .out_4(byte_2_out_4));
  \byte  byte_3 (.A(and_3_out), .WE(WE), .in_2(in_2), .out_4(byte_3_out_4));
  \byte  byte_4 (.A(and_4_out), .WE(WE), .in_2(in_2), .out_4(byte_4_out_4));
  assign out_5 = byte_4_out_4 | byte_3_out_4 | byte_2_out_4 | byte_1_out_4;  // OR_Gate or_1, 8 bits wide
endmodule

module bank8 (
  input  [7:0] in_1,
  input  WE,
  input  [2:0] A,
  output [7:0] out_4
);

  wire not_1_out;
  wire [7:0] bank4_1_out_5, bank4_2_out_5;

  not not_1 (not_1_out, A[2]);
  bank4 bank4_1 (.A(A[1:0]), .b(not_1_out), .WE(WE), .in_2(in_1), .out_5(bank4_1_out_5));
  bank4 bank4_2 (.A(A[1:0]), .b(A[2]), .WE(WE), .in_2(in_1), .out_5(bank4_2_out_5));
  Hex_Digit_Display hex_digit_display_1 (.value(in_1[7:4]));  // open: dp
  Hex_Digit_Display hex_digit_display_2 (.value(in_1[3:0]));  // open: dp
  assign out_4 = bank4_2_out_5 | bank4_1_out_5;  // OR_Gate or_1, 8 bits wide
  Hex_Digit_Display hex_digit_display_3 (.value(out_4[7:4]));  // open: dp
  Hex_Digit_Display hex_digit_display_4 (.value(out_4[3:0]));  // open: dp
endmodule
