// Logisim project multiplexerKP.circ as structural Verilog: 2 circuits, main circuit mux8
module mux8 (
  input  A,
  input  B,
  input  [7:0] in_3,
  input  [7:0] in_4,
  input  [7:0] in_5,
  input  [7:0] in_6,
  input  S,
  input  [1:0] in_8,
  output Out,
  output [7:0] out_10
);

  wire and_5_out, and_6_out;
  wire [7:0] and_1_out, and_2_out, and_3_out, and_4_out, selector_1_out_2, selector_1_out_3;

  assign and_1_out = in_3 & selector_1_out_3 & selector_1_out_2;  // AND_Gate and_1, 8 bits wide
  Hex_Digit_Display hex_digit_display_1 (.value(in_3[7:4]));  // open: dp
  Hex_Digit_Display hex_digit_display_2 (.value(in_3[3:0]));  // open: dp
  assign and_2_out = in_4 & selector_1_out_3 & ~selector_1_out_2;  // AND_Gate and_2, 8 bits wide
  Hex_Digit_Display hex_digit_display_3 (.value(in_4[7:4]));  // open: dp
  Hex_Digit_Display hex_digit_display_4 (.value(in_4[3:0]));  // open: dp
  assign out_10 = and_1_out | and_2_out | and_3_out | and_4_out;  // OR_Gate or_1, 8 bits wide
  Hex_Digit_Display hex_digit_display_5 (.value(in_5[7:4]));  // open: dp
  assign and_3_out = in_5 & ~selector_1_out_3 & selector_1_out_2;  // AND_Gate and_3, 8 bits wide
  Hex_Digit_Display hex_digit_display_6 (.value(out_10[7:4]));  // open: dp
  Hex_Digit_Display hex_digit_display_7 (.value(in_5[3:0]));  // open: dp
  Hex_Digit_Display hex_digit_display_8 (.value(out_10[3:0]));  // open: dp
  Hex_Digit_Display hex_digit_display_9 (.value(in_6[7:4]));  // open: dp
  assign and_4_out = in_6 & ~selector_1_out_3 & ~selector_1_out_2;  // AND_Gate and_4, 8 bits wide
  Hex_Digit_Display hex_digit_display_10 (.value(in_6[3:0]));  // open: dp
  selector selector_1 (.out_2(selector_1_out_2), .out_3(selector_1_out_3), .in_1(in_8));
  and and_5 (and_5_out, A, ~S);  // AND_Gate
  and and_6 (and_6_out, B, S);
  or or_2 (Out, and_5_out, and_6_out);

  // Notes on the sheet:
  //   multiplexerKP
  //   Warmup
endmodule

module selector (
  input  [1:0] in_1,
  output [7:0] out_2,
  output [7:0] out_3
);


  assign out_2 = {8{in_1[0]}};
  assign out_3 = {8{in_1[1]}};
endmodule
